# Fritzing sketch tutorial 9 - Temperatura (saved by Fritzing 0.9.3b)
breadboards: 1

parts:
  Componente1 = Arduino Mega 2560 (Rev3)
  DS1 = DS18B20 1-Wire Temperature Sensor [part_number=DS18B20]
  R1 = Resistor [tolerance=±5% resistance=4.7k package=THT]

nets:
  5V: Componente1.5V, DS1.VDD, R1.Pin_0
  GND: Componente1.GND, DS1.GND
  N1: Componente1.D2_PWM, DS1.DQ, R1.Pin_1
